# Fritzing sketch IR Wiring (saved by Fritzing 0.9.3b)
breadboards: 1

parts:
  Part1 = Arduino Uno (Rev3)
  IR1 = TSOP312.., 314.. [package=THT]
  LED1 = smd LED [color="Green (555nm)" package="0603 [SMD]"]
  LED2 = smd LED [color="Orange (620nm)" package="0603 [SMD]"]
  LED3 = smd LED [color="Red (633nm)" package="0603 [SMD]"]

nets:
  N1: Part1.D8, LED3.anode
  N2: Part1.D10_PWM/SS, LED2.anode
  N3: Part1.D12/MISO, LED1.anode
  N4: Part1.D13/SCK, IR1.GND
  N5: Part1.5V, IR1.Data
  N6: Part1.GND, IR1.Vs, LED1.cathode, LED2.cathode, LED3.cathode
